# Fritzing sketch Arduino Pro Mini SD-TFT Hookup (saved by Fritzing 1.0.7)
breadboards: 1

parts:
  Part1 = Arduino Mega 2560 (Rev3)  # not connected
  Part2 = Adafruit AS7341  # not connected
  S1 = SWITCH-MOMENTARY-2 [package=tactile-pth-12mm]  # not connected
  S2 = SWITCH-MOMENTARY-2 [package=tactile-pth-12mm]  # not connected
  S3 = SWITCH-MOMENTARY-2 [package=tactile-pth-12mm]  # not connected
  U1 = Thumb Joystick [package=joystick]  # not connected
  R4 = Resistor [tolerance=±5% power=0.25W resistance=680 package=THT]
  R5 = Resistor [tolerance=±5% power=0.25W resistance=680 package=THT]
  R6 = Resistor [tolerance=±5% power=0.25W resistance=680 package=THT]
  R7 = Resistor [tolerance=±5% power=0.25W resistance=680 package=THT]
  R8 = Resistor [tolerance=±5% power=0.25W resistance=680 package=THT]
  R9 = Resistor [tolerance=±5% power=0.25W resistance=680 package=THT]
  R13 = Resistor [tolerance=±5% power=0.25W resistance=330 package=THT]
  R14 = Resistor [tolerance=±5% power=0.25W resistance=330 package=THT]
  R15 = Resistor [tolerance=±5% power=0.25W resistance=330 package=THT]
  R16 = Resistor [tolerance=±5% power=0.25W resistance=330 package=THT]
  R17 = Resistor [tolerance=±5% power=0.25W resistance=330 package=THT]
  R18 = Resistor [tolerance=±5% power=0.25W resistance=330 package=THT]
  LCD1 = TFT 1.8 inch 160x128 w SD
  Part3 = Arduino Pro Mini (3.3V)  # not connected

nets:
  N1: R4.Pin_0, R5.Pin_0, R6.Pin_0, R7.Pin_0, R8.Pin_0, R9.Pin_0, LCD1.pin2
  N2: R4.Pin_1, R13.Pin_0, LCD1.pin_9
  N3: R5.Pin_1, R14.Pin_0, LCD1.pin4
  N4: R6.Pin_1, R15.Pin_0, LCD1.pin_7, LCD1.pin_12
  N5: R7.Pin_1, R16.Pin_0, LCD1.pin_6, LCD1.pin_10
  N6: R8.Pin_1, R17.Pin_0, LCD1.pin_5
  N7: R9.Pin_1, R18.Pin_0, LCD1.pin3
  N8: LCD1.pin_1, LCD1.pin_8

custom parts:
  TFT 1.8 inch 160x128 w SD: This is a generic 1.8 tft spi lcd display available on ebay and others. The 1.8" display has 128x160 color pixels and in this version pin names in breadboard (unlike the real board).
