# Fritzing sketch Complete Circuit (saved by Fritzing 1.0.7)
breadboards: 1

parts:
  AT_Mega_2560 = Arduino Mega 2560 (Rev3)
  LCD1 = TFT 1.8 inch 160x128 w SD
  AS7341_Spectometer = Adafruit AS7341
  Clock = ZS-042 RTC Module
  R1 = Resistor [tolerance=±5% power=0.25W resistance=330 package=THT]
  R2 = Resistor [tolerance=±5% power=0.25W resistance=680 package=THT]
  U1 = Thumb Joystick [package=joystick]
  V1 = DC Power [voltage=9V internal_resistance=0.1Ω]
  R3 = Resistor [tolerance=±5% power=0.25W resistance=330 package=THT]
  R4 = Resistor [tolerance=±5% power=0.25W resistance=680 package=THT]
  R5 = Resistor [tolerance=±5% power=0.25W resistance=330 package=THT]
  R6 = Resistor [tolerance=±5% power=0.25W resistance=680 package=THT]
  R7 = Resistor [tolerance=±5% power=0.25W resistance=330 package=THT]
  R8 = Resistor [tolerance=±5% power=0.25W resistance=680 package=THT]
  R9 = Resistor [tolerance=±5% power=0.25W resistance=330 package=THT]
  R10 = Resistor [tolerance=±5% power=0.25W resistance=680 package=THT]
  R11 = Resistor [tolerance=±5% power=0.25W resistance=680 package=THT]
  R12 = Resistor [tolerance=±5% power=0.25W resistance=330 package=THT]
  BACK = Momentary Switch [package=ksa_sealed_tac_switch]
  VIEW = Momentary Switch [package=ksa_sealed_tac_switch]
  SETTINGS = Momentary Switch [package=ksa_sealed_tac_switch]
  R13 = Resistor [tolerance=±5% power=0.25W resistance=68 package=THT]

nets:
  N1: AT_Mega_2560.A0, U1.V
  N2: AT_Mega_2560.A1, U1.H
  N3: AT_Mega_2560.D21/SCL, AT_Mega_2560.SCL, AS7341_Spectometer.SCL, Clock.SCL
  N4: AT_Mega_2560.D20/SDA, AT_Mega_2560.SDA, AS7341_Spectometer.SDA, Clock.SDA
  GND: AT_Mega_2560.GND, LCD1.pin2, AS7341_Spectometer.GND, Clock.GND, R2.Pin_0, U1.SEL-, U1.H-, U1.V-, V1.V-, R4.Pin_0, R6.Pin_0, R8.Pin_0, R10.Pin_0, R11.Pin_0, BACK.3, BACK.4, VIEW.3, VIEW.4, SETTINGS.3, SETTINGS.4
  9V: AT_Mega_2560.VIN, V1.V+
  N5: AT_Mega_2560.D4_PWM, R7.Pin_1, R8.Pin_1
  N6: AT_Mega_2560.D5_PWM, R11.Pin_1, R12.Pin_1
  N7: AT_Mega_2560.D6_PWM, R9.Pin_1, R10.Pin_1
  N8: AT_Mega_2560.D7_PWM, R5.Pin_1, R6.Pin_1
  5V: AT_Mega_2560.5V
  N9: AT_Mega_2560.D22, U1.SEL+
  N10: AT_Mega_2560.D23, BACK.1, BACK.2
  N11: AT_Mega_2560.D24, VIEW.1, VIEW.2
  N12: AT_Mega_2560.D25, SETTINGS.1, SETTINGS.2
  N13: AT_Mega_2560.D44, R13.Pin_1
  N14: AT_Mega_2560.D50, LCD1.pin_11
  N15: AT_Mega_2560.D51, R3.Pin_1, R4.Pin_1
  N16: AT_Mega_2560.D52, R1.Pin_1, R2.Pin_1
  VCC: LCD1.pin_1, AS7341_Spectometer.VCC, Clock.VCC, U1.V+, U1.H+
  TFT CS: LCD1.pin3, R5.Pin_0
  reset: LCD1.pin4, R12.Pin_0
  RS: LCD1.pin_5, R9.Pin_0
  SDA/MOSI: LCD1.pin_6, LCD1.pin_10, R3.Pin_0
  SCK/CLK: LCD1.pin_7, LCD1.pin_12, R1.Pin_0
  BL: LCD1.pin_8, R13.Pin_0
  SD CS: LCD1.pin_9, R7.Pin_0

notes:
  3.3v Logic

custom parts:
  TFT 1.8 inch 160x128 w SD: This is a generic 1.8 tft spi lcd display available on ebay and others. The 1.8" display has 128x160 color pixels and in this version pin names in breadboard (unlike the real board).
